# Fritzing sketch TMC2130_breakout (saved by Fritzing 0.9.2b)
circuit board: 4.99999cm x 2.94cm
breadboards: 1

parts:
  E0 = male pin header, 4 pins [form="♂ (male)"]
  Z = male pin header, 4 pins [form="♂ (male)"]
  Y = male pin header, 4 pins [form="♂ (male)"]
  X = male pin header, 4 pins [form="♂ (male)"]
  SC = male pin header, 3 pins [form="♂ (male)"]
  CS = male pin header, 4 pins [form="♂ (male)"]

nets:
  N1: E0.pin1, Z.pin1, Y.pin1, X.pin1, SC.pin1
  N2: E0.pin2, Z.pin2, Y.pin2, X.pin2, SC.pin2
  N3: E0.pin3, CS.pin4
  N4: E0.pin4, Z.pin4, Y.pin4, X.pin4, SC.pin3
  N5: Z.pin3, CS.pin3
  N6: Y.pin3, CS.pin2
  N7: X.pin3, CS.pin1

notes:
  SDI
  SCK
  SDO
  CS
  E0
  Z
  Y
  X
  -
